# Fritzing sketch boat (saved by Fritzing 1.0.4)

parts:
  Mod1 = Raspberry Pi Pico
  M6 = Dagu DGServo 9g (Top view) [part_number=RS001B]
  A1 = fs R6A
  IC1 = DIP - 6 pins [chip_label="20A ECS" package="DIP (Dual Inline) [THT]"]
  U1 = LIPO-11.1V-3 Cells [package=Li-Po-2200]
  A2 = DYS BE1806
  M7 = RioRand LM2596

nets:
  N1: Mod1.pin_3, Mod1.pin_28, Mod1.pin_33, Mod1.pin_38, M6.gnd, A1.Pin_1, M7.Pin_4
  N2: Mod1.pin_4, M6.pulse
  N3: Mod1.pin_6, IC1.In
  N4: Mod1.pin_7, A1.Pin_3
  N5: Mod1.pin_39, M7.Pin_3
  N6: Mod1.pin_40, M6.vcc, A1.Pin_2
  N7: IC1.V+, U1.+, M7.Pin_1
  N8: IC1.GND, U1.-, M7.Pin_2
  N9: IC1.A, A2.Pin_1
  N10: IC1.B, A2.Pin_2
  N11: IC1.C, A2.Pin_3

custom parts:
  Raspberry Pi Pico: Raspberry Pi Pico. Based around the RP2040 microcontroller the Pico is a low cost microcontroller device bringing Raspberry Pi quality, cost, and easy of use to the microcontroller space. Jan 2021, Split part in to two versions: tht (this one) and SMD. This one will drill holes for a .1 in header in pcb to allow plugging in the module as well as providing pads to solder the module to the top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
  fs R6A: FS R6A RC receiver.
  DIP - 6 pins: 20A ECS with only single IN
  LIPO-11.1V-3 Cells: Li-Po Battery-11.1V-3Cells-2200mAh
  DYS BE1806: quadcopter brushless motor.
